// Logisim project demo2.circ as structural Verilog: 11 circuits, main circuit main
module main (
  input  [3:0] Register_Number,
  input  Reset,
  output [31:0] out_3,
  output [31:0] out_4,
  output [31:0] out_5,
  output [31:0] out_6,
  output [23:0] out_7,
  output [31:0] out_8,
  output [23:0] out_9,
  output [31:0] out_10,
  output [3:0] out_11,
  output [31:0] out_12,
  output [31:0] out_13,
  output [31:0] out_14,
  output [31:0] out_15,
  output [31:0] out_16,
  output [31:0] out_17,
  output [31:0] out_18,
  output [31:0] out_19
);

  wire Act_EX, Act_MA, Act_RW, and_1_out, and_2_out, and_3_out, and_4_out, and_5_out, and_6_out, and_7_out,
       and_8_out, CLOCK, CLOCK_t, forwarding_unit_1_fwdr2, forwarding_unit_1_isconflict,
       forwarding_unit_2_fwdr1, forwarding_unit_2_fwdr2, forwarding_unit_2_isconflict,
       forwarding_unit_3_fwdr1, forwarding_unit_3_fwdr2, forwarding_unit_3_isconflict,
       forwarding_unit_4_fwdr1, forwarding_unit_4_fwdr2, forwarding_unit_4_isconflict, Is_conflict, isBeq,
       isBeq_EX, isBeq_MA, isBeq_RW, isBgt, isBgt_EX, isBgt_MA, isBgt_RW, isBranchTaken, isCall, isCall_EX,
       isCall_MA, isCall_RW, isImmediate, isImmediate_EX, isImmediate_MA, isImmediate_RW, isLd, isLd_EX,
       isLd_MA, isLd_RW, isRet, isRet_EX, isRet_MA, isRet_RW, isSt, isSt_EX, isSt_MA, isSt_RW, isUbranch,
       isUbranch_EX, isUbranch_MA, isUbranch_RW, isWb, isWb_EX, isWb_MA, isWb_RW, or_1_out, or_2_out,
       register_1_q;
  wire [3:0] aluSignals, aluSignals_EX, aluSignals_MA, aluSignals_RW, of_1_displayout, of_1_displayout_2,
       of_1_displayout_3, of_1_displayout_4, of_1_displayout_5, of_1_displayout_6, of_1_displayout_7,
       of_1_displayout_8;
  wire [12:0] multiplexer_18_out;
  wire [23:0] branchPC, multiplexer_2_out, PC_EX, PC_MA, PC_OF, PC_RW;
  wire [31:0] A, A_EX, A_new, aluResult, aluResult_RW, B_EX, bT, bT_EX, bT_out, immx_out, Inp_A, Inp_A_EX,
       Inp_B, Inp_B_EX, Inp_B_out, Inp_op2_EX, Inst_OF_out, Int_A_EX, Int_B_EX, ldResult_RW,
       multiplexer_1_out, multiplexer_3_out, op2, op2_Inp_EX, op2_MA, op2_new, return_address;

  Clock u_Clock (.out(CLOCK));
  Register #(.width(1)) register_1 (.D(isBranchTaken), .Q(register_1_q), .clk(CLOCK));  // open: en, clr
  Multiplexer #(.width(32), .enable("false")) multiplexer_1 (
    .in0(out_10), .in1(out_4), .out(multiplexer_1_out), .sel(Is_conflict));
  Multiplexer #(.width(24), .enable("false")) multiplexer_2 (
    .in0(out_9), .in1(PC_OF), .out(multiplexer_2_out), .sel(Is_conflict));
  Register #(.width(24)) register_2 (.D(branchPC), .Q(out_7), .clk(CLOCK));  // open: en, clr
  MA ma_1 (.ldResult(out_14), .op2(out_13), .isLd(isLd_MA), .isSt(isSt_MA), .ALUResult(out_15), .Clock(CLOCK));
  Register #(.width(24)) register_3 (.D(multiplexer_2_out), .Q(PC_OF), .clk(CLOCK));  // open: en, clr
  IF if_1 (
    .isBranchTaken(register_1_q), .Instruction(out_10), .branchTarget(out_7), .IFstageclock(CLOCK),
    .PC(out_9), .reset(Reset), .Is_conflict(Is_conflict));
  Multiplexer #(.width(32), .enable("false")) multiplexer_3 (
    .in0(multiplexer_1_out), .in1(32'h68000000), .out(multiplexer_3_out), .sel(isBranchTaken));
  Register #(.width(32)) register_4 (.D(op2_new), .Q(out_18), .clk(CLOCK));  // open: en, clr
  Register #(.width(32)) register_5 (.D(aluResult), .Q(out_15), .clk(CLOCK));  // open: en, clr
  Register #(.width(32)) register_6 (.D(bT), .Q(bT_EX), .clk(CLOCK));  // open: en, clr
  Register #(.width(32)) register_7 (.D(out_14), .Q(ldResult_RW), .clk(CLOCK));  // open: en, clr
  Forwarding_unit forwarding_unit_1 (
    .instr_A(out_3), .Insr_B(out_5), .RA(return_address), .FwdR2(forwarding_unit_1_fwdr2),
    .isConflict(forwarding_unit_1_isconflict));  // open: FwdR1
  Forwarding_unit forwarding_unit_2 (
    .instr_A(out_6), .Insr_B(out_5), .RA(return_address), .FwdR2(forwarding_unit_2_fwdr2),
    .FwdR1(forwarding_unit_2_fwdr1), .isConflict(forwarding_unit_2_isconflict));
  and and_1 (and_1_out, forwarding_unit_2_isconflict, forwarding_unit_2_fwdr2, Act_RW);
  Data_lock_unit data_lock_unit_1 (
    .A_instruction(out_4), .B_instruction(out_6), .Is_conflict(Is_conflict), .hasReached2(Act_MA),
    .clock(CLOCK), .reset(Reset), .hasReached1(Act_EX), .hasReached3(Act_RW));
  Register #(.width(32)) register_8 (.D(multiplexer_3_out), .Q(out_4), .clk(CLOCK));  // open: en, clr
  Register #(.width(24)) register_9 (.D(PC_OF), .Q(PC_EX), .clk(CLOCK));  // open: en, clr
  Multiplexer #(.width(32)) multiplexer_4 (.in0(op2_MA), .in1(out_12), .out(out_13), .sel(and_2_out));  // open: en
  and and_2 (and_2_out, and_3_out, Act_RW);
  and and_3 (and_3_out, forwarding_unit_1_fwdr2, forwarding_unit_1_isconflict);
  Multiplexer #(.width(32)) multiplexer_5 (.in0(A_EX), .in1(out_12), .out(Int_A_EX), .sel(and_4_out));  // open: en
  and and_4 (and_4_out, forwarding_unit_2_fwdr1, forwarding_unit_2_isconflict, Act_RW);
  Multiplexer #(.width(32)) multiplexer_6 (.in0(B_EX), .in1(out_12), .out(Int_B_EX), .sel(and_1_out));  // open: en
  Multiplexer #(.width(32)) multiplexer_7 (.in0(out_18), .in1(out_12), .out(Inp_op2_EX), .sel(and_1_out));  // open: en
  Register #(.width(32)) register_10 (.D(Inst_OF_out), .Q(out_6), .clk(CLOCK));  // open: en, clr
  Register #(.width(24)) register_11 (.D(PC_EX), .Q(PC_MA), .clk(CLOCK));  // open: en, clr
  Register #(.width(32)) register_12 (.D(Inp_op2_EX), .Q(op2_MA), .clk(CLOCK));  // open: en, clr
  Register #(.width(32)) register_13 (.D(out_15), .Q(aluResult_RW), .clk(CLOCK));  // open: en, clr
  Register #(.width(32)) register_14 (.D(A_new), .Q(A_EX), .clk(CLOCK));  // open: en, clr
  Register #(.width(32)) register_15 (.D(Inp_B_out), .Q(B_EX), .clk(CLOCK));  // open: en, clr
  OF of_1 (
    .Instruction(out_4), .PC(PC_OF), .branchTarget(bT_out), .isSt(isSt), .A(A), .Immx(immx_out), .op2(op2),
    .isRet(isRet), .writeData(out_12), .writeAddress(out_11), .isWb(isWb_RW), .clock(CLOCK),
    .displayAddress(Register_Number),
    .displayOut({of_1_displayout_8, of_1_displayout_7, of_1_displayout_6, of_1_displayout_5, of_1_displayout_4, of_1_displayout_3, of_1_displayout_2, of_1_displayout}),
    .isCall(isCall_RW), .ra(return_address));
  Forwarding_unit forwarding_unit_3 (
    .instr_A(out_6), .Insr_B(out_3), .RA(return_address), .FwdR2(forwarding_unit_3_fwdr2),
    .FwdR1(forwarding_unit_3_fwdr1), .isConflict(forwarding_unit_3_isconflict));
  and and_5 (and_5_out, forwarding_unit_3_isconflict, forwarding_unit_3_fwdr2, Act_MA);
  EXU exu_1 (
    .isBeq(isBeq_EX), .isUbranch(isUbranch_EX), .isBgt(isBgt_EX), .branchTargetIn(bT_EX), .A(Inp_A_EX),
    .aluSignals(aluSignals_EX), .B(Inp_B_EX), .Clock(CLOCK), .isBranchTaken(isBranchTaken),
    .branchTargetOut(branchPC), .ALUResult(aluResult), .isRet(isRet_EX));
  Register #(.width(32)) register_16 (.D(out_6), .Q(out_3), .clk(CLOCK));  // open: en, clr
  Register #(.width(24)) register_17 (.D(PC_MA), .Q(PC_RW), .clk(CLOCK));  // open: en, clr
  Multiplexer #(.width(32)) multiplexer_8 (.in0(Int_A_EX), .in1(out_15), .out(Inp_A_EX), .sel(and_6_out));  // open: en
  and and_6 (and_6_out, forwarding_unit_3_fwdr1, forwarding_unit_3_isconflict, Act_MA);
  Multiplexer #(.width(32)) multiplexer_9 (.in0(Int_B_EX), .in1(out_15), .out(Inp_B_EX), .sel(and_5_out));  // open: en
  Forwarding_unit forwarding_unit_4 (
    .instr_A(out_4), .Insr_B(out_5), .RA(return_address), .FwdR2(forwarding_unit_4_fwdr2),
    .FwdR1(forwarding_unit_4_fwdr1), .isConflict(forwarding_unit_4_isconflict));
  and and_7 (and_7_out, forwarding_unit_4_isconflict, forwarding_unit_4_fwdr2, Act_RW);
  Multiplexer #(.width(32), .enable("false")) multiplexer_10 (
    .in0(op2_Inp_EX), .in1(immx_out), .out(Inp_B), .sel(isImmediate));
  Multiplexer #(.width(32)) multiplexer_11 (.in0(A), .in1(out_12), .out(Inp_A), .sel(and_8_out));  // open: en
  and and_8 (and_8_out, forwarding_unit_4_fwdr1, forwarding_unit_4_isconflict, Act_RW);
  Multiplexer #(.width(32)) multiplexer_12 (.in0(op2), .in1(out_12), .out(op2_Inp_EX), .sel(and_7_out));  // open: en
  RW rw_1 (
    .Instruction(out_5), .ldResult(ldResult_RW), .isLd(isLd_RW), .ALUResult(aluResult_RW),
    .isCall(isCall_RW), .PC(PC_RW), .Address(out_11), .storeData(out_12));
  Register #(.width(32)) register_18 (.D(out_3), .Q(out_5), .clk(CLOCK));  // open: en, clr
  Multiplexer #(.width(32), .enable("false")) multiplexer_13 (
    .in0(Inp_B), .in1({32{1'b0}}), .out(Inp_B_out), .sel(or_2_out));
  Multiplexer #(.width(32), .enable("false")) multiplexer_14 (.in0(bT_out), .in1({32{1'b0}}), .out(bT), .sel(or_2_out));
  Multiplexer #(.width(32), .enable("false")) multiplexer_15 (
    .in0(op2_Inp_EX), .in1({32{1'b0}}), .out(op2_new), .sel(or_2_out));
  Multiplexer #(.width(32), .enable("false")) multiplexer_16 (
    .in0(Inp_A), .in1({32{1'b0}}), .out(A_new), .sel(or_2_out));
  Multiplexer #(.width(32), .enable("false")) multiplexer_17 (
    .in0(out_4), .in1(32'h68000000), .out(Inst_OF_out), .sel(or_2_out));
  Hex_Digit_Display hex_digit_display_1 (.value(of_1_displayout_8));  // open: dp
  Hex_Digit_Display hex_digit_display_2 (.value(of_1_displayout_6));  // open: dp
  Hex_Digit_Display hex_digit_display_3 (.value(of_1_displayout_7));  // open: dp
  CU cu_1 (
    .isWb(isWb), .isUbranch(isUbranch), .isImmediate(isImmediate), .isLd(isLd), .isSt(isSt), .isBeq(isBeq),
    .isBgt(isBgt), .isCall(isCall), .isRet(isRet), .ALUSignals(aluSignals), .Instruction(out_4));
  or or_1 (or_1_out, Is_conflict, isBranchTaken);
  Multiplexer #(.width(13), .enable("false")) multiplexer_18 (
    .in0({isSt, isBgt, isCall, isRet, isBeq, isLd, aluSignals, isImmediate, isUbranch, isWb}),
    .in1({13{1'b0}}), .out(multiplexer_18_out), .sel(or_1_out));
  Register #(.width(13)) register_19 (
    .D(multiplexer_18_out),
    .Q({isSt_EX, isBgt_EX, isCall_EX, isRet_EX, isBeq_EX, isLd_EX, aluSignals_EX, isImmediate_EX, isUbranch_EX, isWb_EX}),
    .clk(CLOCK_t));  // open: en, clr
  Register #(.width(13)) register_20 (
    .D({isSt_EX, isBgt_EX, isCall_EX, isRet_EX, isBeq_EX, isLd_EX, aluSignals_EX, isImmediate_EX, isUbranch_EX, isWb_EX}),
    .Q({isSt_MA, isBgt_MA, isCall_MA, isRet_MA, isBeq_MA, isLd_MA, aluSignals_MA, isImmediate_MA, isUbranch_MA, isWb_MA}),
    .clk(CLOCK_t));  // open: en, clr
  Register #(.width(13)) register_21 (
    .D({isSt_MA, isBgt_MA, isCall_MA, isRet_MA, isBeq_MA, isLd_MA, aluSignals_MA, isImmediate, isUbranch, isWb_MA}),
    .Q({isSt_RW, isBgt_RW, isCall_RW, isRet_RW, isBeq_RW, isLd_RW, aluSignals_RW, isImmediate_RW, isUbranch_RW, isWb_RW}),
    .clk(CLOCK_t));  // open: en, clr
  Hex_Digit_Display hex_digit_display_4 (.value(of_1_displayout_4));  // open: dp
  Hex_Digit_Display hex_digit_display_5 (.value(of_1_displayout_5));  // open: dp
  or or_2 (or_2_out, Is_conflict, isBranchTaken);
  Hex_Digit_Display hex_digit_display_6 (.value(of_1_displayout_3));  // open: dp
  Hex_Digit_Display hex_digit_display_7 (.value(of_1_displayout_2));  // open: dp
  Hex_Digit_Display hex_digit_display_8 (.value(of_1_displayout));  // open: dp

  assign out_8 = out_5;
  assign out_16 = out_3;
  assign out_17 = out_6;
  assign out_19 = out_12;

  // Other names for the same wires on the sheet: Address[3:0] = out_11; aluResult_MA[31:0] = out_15;
  //   Inp_op2_MA[31:0] = out_13; Inst_EX[31:0] = out_6; Inst_MA[31:0] = out_3; Inst_OF[31:0] = out_4;
  //   Inst_RW[31:0] = out_5; Instruction[31:0] = out_10; ldResult[31:0] = out_14; op2_EX[31:0] = out_18;
  //   PC[23:0] = out_9; storeData[31:0] = out_12

  // Notes on the sheet:
  //   Changes made to
  //   Inputs, Registers &
  //   Forwarding Block
  //   May be an error,maybe one is add
  //   Nop
  //   Forwading Blocks
  //   MA-RW fwd
  //   MA-RW
  //   EX-RW
  //   Ex-RW fwd
  //   Int_blank -> intermidiate result
  //   Note: The last instruction should be provided as "ffffffff" otherwise it will keep on interpreting "00000000", i.e. it will keep on doubling r0.
  //   Inp_blank -> Input for stage
  //   EX-MA
  //   MA-EX fwd
  //   OF-RW
  //   OF-RW fwd
  //   Nop
  //   Nop
endmodule

module IF (
  input  [23:0] branchTarget,
  input  isBranchTaken,
  input  Is_conflict,
  input  IFstageclock,
  input  reset,
  output [31:0] Instruction,
  output [23:0] PC
);

  wire and_1_out, and_2_out, and_3_out, multiplexer_1_out, not_1_out, not_2_out, not_3_out, not_4_out;

  not not_1 (not_1_out, isBranchTaken);
  not not_2 (not_2_out, Is_conflict);
  not not_3 (not_3_out, IFstageclock);
  and and_1 (and_1_out, not_1_out, not_2_out);
  Multiplexer #(.enable("false")) multiplexer_1 (.in0(not_3_out), .in1(1'b1), .out(multiplexer_1_out), .sel(and_2_out));
  and and_2 (and_2_out, and_3_out, not_4_out);
  Counter #(.width(24), .max('hffffff)) counter_1 (
    .load(isBranchTaken), .D(branchTarget), .count(and_1_out), .Q(PC), .clk(multiplexer_1_out), .clr(reset));  // open: carry
  not not_4 (not_4_out, isBranchTaken);
  ROM #(.addrWidth(24), .dataWidth(32)) rom_1 (.addr(PC), .data(Instruction));  // open: sel
  and and_3 (and_3_out, Instruction[31], Instruction[30], Instruction[29], Instruction[28], Instruction[27], Instruction[26], Instruction[25], Instruction[24], Instruction[23], Instruction[22], Instruction[21], Instruction[20], Instruction[19], Instruction[18], Instruction[17], Instruction[16], Instruction[14], Instruction[13], Instruction[12], Instruction[11], Instruction[10], Instruction[9], Instruction[8], Instruction[7], Instruction[6], Instruction[5], Instruction[4], Instruction[3], Instruction[2], Instruction[1], Instruction[0], Instruction[15]);

  // Other names for the same wires on the sheet: brT = isBranchTaken

  // Notes on the sheet:
  //   reset: pull=down
  //   IF Stage
  //   Counter for going to the next instruction
  //   Note: The last instruction should be provided as "ffffffff" otherwise it will keep on interpreting "00000000", i.e. it will keep on doubling r0.
  //   contents of rom_1 (hex, n*v repeats v):
  //   4c000173 4c400000 48800000 4d400000 90000007 24c8000a 110cc000 1110c000 1550000 1c88000a 90000001
  //   2c080000 8ffffff9 80000001 28140000 80000002 90000002 4c400001 90000000
  //   Used to stop instruction processing on encountering code "ffffffff".
endmodule

module OF (
  input  isRet,
  input  [23:0] PC,
  input  [31:0] Instruction,
  input  isCall,
  input  [3:0] writeAddress,
  input  [31:0] writeData,
  input  isWb,
  input  clock,
  input  isSt,
  input  [3:0] displayAddress,
  output [31:0] A,
  output [31:0] op2,
  output [31:0] Immx,
  output [31:0] ra,
  output [31:0] displayOut,
  output [31:0] branchTarget
);

  wire and_1_out, not_1_out, or_1_out;
  wire [3:0] multiplexer_2_out, multiplexer_3_out;
  wire [31:0] adder_1_out, bit_extender_1_out, bit_extender_2_out, bit_extender_3_out, bit_extender_4_out,
       shifter_1_out;

  assign bit_extender_1_out = {{5{Instruction[26]}}, Instruction[26:0]};  // Bit_Extender bit_extender_1
  assign bit_extender_2_out = {{8{1'b0}}, PC};  // Bit_Extender bit_extender_2
  Multiplexer #(.width(32), .enable("false")) multiplexer_1 (
    .in0(adder_1_out), .in1(A), .out(branchTarget), .sel(isRet));
  Adder #(.width(32)) adder_1 (.a(bit_extender_1_out), .b(bit_extender_2_out), .out(adder_1_out));  // open: cin, cout
  assign bit_extender_3_out = {{16{Instruction[15]}}, Instruction[15:0]};  // Bit_Extender bit_extender_3
  assign bit_extender_4_out = {{16{1'b0}}, Instruction[15:0]};  // Bit_Extender bit_extender_4
  Shifter #(.width(32)) shifter_1 (.in(bit_extender_4_out), .\dist (5'b10000), .out(shifter_1_out));
  Multiplexer #(.width(4), .enable("false")) multiplexer_2 (
    .in0(Instruction[21:18]), .in1(4'b1111), .out(multiplexer_2_out), .sel(isRet));
  Multiplexer #(.width(4), .enable("false")) multiplexer_3 (
    .in0(Instruction[17:14]), .in1(Instruction[25:22]), .out(multiplexer_3_out), .sel(isSt));
  Multiplexer #(.select(2), .width(32), .enable("false")) multiplexer_4 (
    .in0(bit_extender_3_out), .in1(bit_extender_4_out), .in2(shifter_1_out), .out(Immx),
    .sel(Instruction[17:16]));  // open: in3
  regFile regfile_1 (
    .writeData(writeData), .writeAddress(writeAddress), .clock(and_1_out), .readB(multiplexer_3_out),
    .outB(op2), .outA(A), .readA(multiplexer_2_out), .displayOut(displayOut), .displayRead(displayAddress),
    .out_10(ra));
  and and_1 (and_1_out, or_1_out, not_1_out);
  or or_1 (or_1_out, isCall, isWb);
  not not_1 (not_1_out, clock);

  // Notes on the sheet:
  //   (Branch Target Calculation)
  //   (27 bit offset)
  //   OF Stage (Edited)
  //   (has Return Address
  //   when instruction is ret)
  //   (Registers from RW Stage moved here to maintain consistency)
  //   rs1
  //   rs2
  //   rd
  //   (modifier bits)
  //   19:22
  //   15:18
  //   23:26
  //   (Immediate Calculation)
  //   (no modifier)
  //   (modifier u)
  //   (modifier h)
  //   (Register Access)
  //   (32 bit modifed immediate)
  //   (OF Outputs)
endmodule

module MA (
  input  [31:0] ALUResult,
  input  isLd,
  input  Clock,
  input  isSt,
  input  [31:0] op2,
  output [31:0] ldResult
);

  wire and_1_out, not_1_out, xor_1_out;
  wire [31:0] shifter_1_out;

  Shifter #(.width(32), .shift("ar")) shifter_1 (.in(ALUResult), .\dist (5'b00010), .out(shifter_1_out));
  and and_1 (and_1_out, isSt, Clock);
  xor xor_1 (xor_1_out, isLd, and_1_out);
  not not_1 (not_1_out, isSt);
  RAM #(.addrWidth(24), .dataWidth(32), .bus("asynch")) ram_1 (
    .addr(shifter_1_out[23:0]), .data(ldResult), .sel(xor_1_out), .ld(not_1_out));  // open: clr
  assign ldResult = isSt ? op2 : 32'bz;  // Controlled_Buffer controlled_buffer_1

  // Notes on the sheet:
  //   MA  Stage
  //   Memory Address
  //   (Data to be stored)
endmodule

module RW (
  input  [31:0] ALUResult,
  input  [31:0] ldResult,
  input  isLd,
  input  [23:0] PC,
  input  isCall,
  input  [31:0] Instruction,
  output [31:0] storeData,
  output [3:0] Address
);

  wire [31:0] adder_1_out, bit_extender_1_out;

  assign bit_extender_1_out = {{8{1'b0}}, PC};  // Bit_Extender bit_extender_1
  Multiplexer #(.width(4), .enable("false")) multiplexer_1 (
    .in0(Instruction[25:22]), .in1(4'b1111), .out(Address), .sel(isCall));
  Adder #(.width(32)) adder_1 (.a(bit_extender_1_out), .b(32'h1), .out(adder_1_out));  // open: cin, cout
  Multiplexer #(.select(2), .width(32), .enable("false")) multiplexer_2 (
    .in0(ALUResult), .in1(ldResult), .in2(adder_1_out), .out(storeData), .sel({isCall, isLd}));  // open: in3

  // Notes on the sheet:
  //   PC: pull=down
  //   Address: pull=down
  //   storeData: pull=down
  //   RW Stage (Edited)
  //   (for arithmetic instructions)
  //   (data loaded from memory)
  //   (to update return address)
  //   (Register to be written to)
  //   (Registers moved to OF Stage to maintain consistency)
  //   (Integer to be written back in register)
endmodule

module regFile (
  input  clock,
  input  [3:0] readA,
  input  [31:0] writeData,
  input  [3:0] readB,
  input  [3:0] writeAddress,
  input  [3:0] displayRead,
  output [31:0] outA,
  output [31:0] outB,
  output [31:0] displayOut,
  output [31:0] out_10
);

  wire counter_1_q;
  wire [31:0] demultiplexer_1_out0, demultiplexer_1_out1, demultiplexer_1_out2, demultiplexer_1_out3,
       demultiplexer_1_out4, demultiplexer_1_out5, demultiplexer_1_out6, demultiplexer_1_out7,
       demultiplexer_1_out8, demultiplexer_1_out9, demultiplexer_1_out10, demultiplexer_1_out11,
       demultiplexer_1_out12, demultiplexer_1_out13, demultiplexer_1_out14, demultiplexer_1_out15,
       multiplexer_1_out, r0, r1, r2, r3, r4, r5, r6, r7, r8, r9, r10, r11, r12, r13, r14;

  Demultiplexer #(.select(4), .width(32), .tristate("true"), .enable("false")) demultiplexer_1 (
    .out0(demultiplexer_1_out0), .out1(demultiplexer_1_out1), .out2(demultiplexer_1_out2),
    .out3(demultiplexer_1_out3), .out4(demultiplexer_1_out4), .out5(demultiplexer_1_out5),
    .out6(demultiplexer_1_out6), .out7(demultiplexer_1_out7), .out8(demultiplexer_1_out8),
    .out9(demultiplexer_1_out9), .out10(demultiplexer_1_out10), .out11(demultiplexer_1_out11),
    .out12(demultiplexer_1_out12), .out13(demultiplexer_1_out13), .out14(demultiplexer_1_out14),
    .out15(demultiplexer_1_out15), .in(writeData), .sel(writeAddress));
  Counter #(.width(1), .max('h1), .ongoal("stay")) counter_1 (
    .Q(counter_1_q), .clk(clock));  // open: load, D, count, carry, clr
  Multiplexer #(.width(32), .enable("false")) multiplexer_1 (
    .in0(32'h3fffffc), .in1(demultiplexer_1_out14), .out(multiplexer_1_out), .sel(counter_1_q));
  Register #(.width(32)) u_r0 (.D(demultiplexer_1_out0), .Q(r0), .clk(clock));  // open: en, clr
  Register #(.width(32)) u_r1 (.D(demultiplexer_1_out1), .Q(r1), .clk(clock));  // open: en, clr
  Register #(.width(32)) u_r2 (.D(demultiplexer_1_out2), .Q(r2), .clk(clock));  // open: en, clr
  Register #(.width(32)) u_r3 (.D(demultiplexer_1_out3), .Q(r3), .clk(clock));  // open: en, clr
  Register #(.width(32)) u_r4 (.D(demultiplexer_1_out4), .Q(r4), .clk(clock));  // open: en, clr
  Register #(.width(32)) u_r5 (.D(demultiplexer_1_out5), .Q(r5), .clk(clock));  // open: en, clr
  Register #(.width(32)) u_r6 (.D(demultiplexer_1_out6), .Q(r6), .clk(clock));  // open: en, clr
  Register #(.width(32)) u_r7 (.D(demultiplexer_1_out7), .Q(r7), .clk(clock));  // open: en, clr
  Register #(.width(32)) u_r8 (.D(demultiplexer_1_out8), .Q(r8), .clk(clock));  // open: en, clr
  Register #(.width(32)) u_r9 (.D(demultiplexer_1_out9), .Q(r9), .clk(clock));  // open: en, clr
  Register #(.width(32)) u_r10 (.D(demultiplexer_1_out10), .Q(r10), .clk(clock));  // open: en, clr
  Register #(.width(32)) u_r11 (.D(demultiplexer_1_out11), .Q(r11), .clk(clock));  // open: en, clr
  Register #(.width(32)) u_r12 (.D(demultiplexer_1_out12), .Q(r12), .clk(clock));  // open: en, clr
  Register #(.width(32)) u_r13 (.D(demultiplexer_1_out13), .Q(r13), .clk(clock));  // open: en, clr
  Register #(.width(32)) u_r14 (.D(multiplexer_1_out), .Q(r14), .clk(clock));  // open: en, clr
  Register #(.width(32)) r15 (.D(demultiplexer_1_out15), .Q(out_10), .clk(clock));  // open: en, clr
  Multiplexer #(.select(4), .width(32), .disabled(0), .enable("false")) multiplexer_2 (
    .in0(r0), .in1(r1), .in2(r2), .in3(r3), .in4(r4), .in5(r5), .in6(r6), .in7(r7), .in8(r8), .in9(r9),
    .in10(r10), .in11(r11), .in12(r12), .in13(r13), .in14(r14), .in15(out_10), .out(outA), .sel(readA));
  Multiplexer #(.select(4), .width(32), .disabled(0), .enable("false")) multiplexer_3 (
    .in0(r0), .in1(r1), .in2(r2), .in3(r3), .in4(r4), .in5(r5), .in6(r6), .in7(r7), .in8(r8), .in9(r9),
    .in10(r10), .in11(r11), .in12(r12), .in13(r13), .in14(r14), .in15(out_10), .out(outB), .sel(readB));
  Multiplexer #(.select(4), .width(32), .disabled(0), .enable("false")) multiplexer_4 (
    .in0(r0), .in1(r1), .in2(r2), .in3(r3), .in4(r4), .in5(r5), .in6(r6), .in7(r7), .in8(r8), .in9(r9),
    .in10(r10), .in11(r11), .in12(r12), .in13(r13), .in14(r14), .in15(out_10), .out(displayOut),
    .sel(displayRead));

  // Other names for the same wires on the sheet: r15[31:0] = out_10

  // Notes on the sheet:
  //   outB: pull=down
  //   readB: pull=down
  //   outA: pull=down
  //   writeData: pull=down
  //   displayRead: pull=down
  //   displayOut: pull=down
  //   readA: pull=down
  //   writeAddress: pull=down
  //   (for RW Stage)
  //   (to initialize stack pointer
  //   to last memory location)
  //   (to fetch Operand 1)
  //   (to fetch Operand 2)
  //   (for external display)
endmodule

module CU (
  input  [31:0] Instruction,
  output isWb,
  output isUbranch,
  output isImmediate,
  output isLd,
  output isSt,
  output isBeq,
  output isBgt,
  output isCall,
  output isRet,
  output [3:0] ALUSignals
);

  wire and_1_out, and_2_out, and_3_out, and_4_out, demultiplexer_1_out0, demultiplexer_1_out1, isAdd, isAnd,
       isAsr, isCmp, isDiv, isLsl, isLsr, isMod, isMov, isMul, isNot, isOr, not_1_out, not_2_out, not_3_out,
       not_4_out, not_5_out, not_6_out, not_7_out, or_1_out, or_2_out;
  wire [3:0] adder_1_out, adder_2_out, adder_3_out, adder_4_out, adder_5_out, adder_6_out, adder_7_out,
       adder_8_out, adder_9_out, adder_10_out, adder_11_out, bit_extender_1_out, bit_extender_2_out,
       bit_extender_3_out, bit_extender_4_out, bit_extender_5_out, bit_extender_6_out, bit_extender_7_out,
       bit_extender_8_out, bit_extender_9_out, bit_extender_10_out, bit_extender_11_out, bit_extender_12_out,
       bit_extender_13_out, multiplier_1_out, multiplier_2_out, multiplier_3_out, multiplier_4_out,
       multiplier_5_out, multiplier_6_out, multiplier_7_out, multiplier_8_out, multiplier_9_out,
       multiplier_10_out, multiplier_11_out, multiplier_12_out;

  not not_1 (not_1_out, Instruction[28]);
  not not_2 (not_2_out, Instruction[29]);
  not not_3 (not_3_out, Instruction[28]);
  not not_4 (not_4_out, Instruction[27]);
  not not_5 (not_5_out, Instruction[31]);
  Demultiplexer #(.select(5), .disabled(0), .enable("false")) demultiplexer_1 (
    .out0(demultiplexer_1_out0), .out1(demultiplexer_1_out1), .out2(isMul), .out3(isDiv), .out4(isMod),
    .out5(isCmp), .out6(isAnd), .out7(isOr), .out8(isNot), .out9(isMov), .out10(isLsl), .out11(isLsr),
    .out12(isAsr), .out14(isLd), .out15(isSt), .out16(isBeq), .out17(isBgt), .out19(isCall), .out20(isRet),
    .in(1'b1), .sel(Instruction[31:27]));  // open: out13, out18, out21, out22, out23, out24, out25, out26, out27, out28, out29, out30, out31
  not not_6 (not_6_out, Instruction[31]);
  or or_1 (or_1_out, Instruction[30], not_1_out);
  and and_1 (and_1_out, not_2_out, Instruction[28]);
  and and_2 (and_2_out, Instruction[29], not_3_out, not_4_out);
  and and_3 (and_3_out, Instruction[28], Instruction[29], Instruction[30], not_5_out);
  and and_4 (and_4_out, not_6_out, Instruction[29], Instruction[27], or_1_out);
  not not_7 (not_7_out, Instruction[30]);
  or or_2 (or_2_out, and_1_out, and_2_out);
  nor nor_1 (isWb, Instruction[31], and_4_out);
  and and_5 (isUbranch, Instruction[31], not_7_out, or_2_out);
  or or_3 (isAdd, and_3_out, demultiplexer_1_out0);
  assign bit_extender_1_out = {{3{1'b0}}, demultiplexer_1_out1};  // Bit_Extender bit_extender_1
  assign bit_extender_2_out = {{3{1'b0}}, isCmp};  // Bit_Extender bit_extender_2
  assign bit_extender_3_out = {{3{1'b0}}, isMul};  // Bit_Extender bit_extender_3
  assign bit_extender_4_out = {{3{1'b0}}, isDiv};  // Bit_Extender bit_extender_4
  assign bit_extender_5_out = {{3{1'b0}}, isMod};  // Bit_Extender bit_extender_5
  assign bit_extender_6_out = {{3{1'b0}}, isLsl};  // Bit_Extender bit_extender_6
  assign bit_extender_7_out = {{3{1'b0}}, isLsr};  // Bit_Extender bit_extender_7
  assign bit_extender_8_out = {{3{1'b0}}, isAsr};  // Bit_Extender bit_extender_8
  assign bit_extender_9_out = {{3{1'b0}}, isOr};  // Bit_Extender bit_extender_9
  assign bit_extender_10_out = {{3{1'b0}}, isNot};  // Bit_Extender bit_extender_10
  assign bit_extender_11_out = {{3{1'b0}}, isAnd};  // Bit_Extender bit_extender_11
  assign bit_extender_12_out = {{3{1'b0}}, isMov};  // Bit_Extender bit_extender_12
  assign bit_extender_13_out = {{3{1'b0}}, isAdd};  // Bit_Extender bit_extender_13
  Multiplier #(.width(4)) multiplier_1 (
    .a(bit_extender_1_out), .b(4'b0010), .out(multiplier_1_out));  // open: cin, cout
  Multiplier #(.width(4)) multiplier_2 (
    .a(bit_extender_2_out), .b(4'b0011), .out(multiplier_2_out));  // open: cin, cout
  Multiplier #(.width(4)) multiplier_3 (
    .a(bit_extender_3_out), .b(4'b0100), .out(multiplier_3_out));  // open: cin, cout
  Multiplier #(.width(4)) multiplier_4 (
    .a(bit_extender_4_out), .b(4'b0101), .out(multiplier_4_out));  // open: cin, cout
  Multiplier #(.width(4)) multiplier_5 (
    .a(bit_extender_5_out), .b(4'b0110), .out(multiplier_5_out));  // open: cin, cout
  Multiplier #(.width(4)) multiplier_6 (
    .a(bit_extender_6_out), .b(4'b0111), .out(multiplier_6_out));  // open: cin, cout
  Multiplier #(.width(4)) multiplier_7 (
    .a(bit_extender_7_out), .b(4'b1000), .out(multiplier_7_out));  // open: cin, cout
  Multiplier #(.width(4)) multiplier_8 (
    .a(bit_extender_8_out), .b(4'b1001), .out(multiplier_8_out));  // open: cin, cout
  Multiplier #(.width(4)) multiplier_9 (
    .a(bit_extender_9_out), .b(4'b1010), .out(multiplier_9_out));  // open: cin, cout
  Multiplier #(.width(4)) multiplier_10 (
    .a(bit_extender_10_out), .b(4'b1011), .out(multiplier_10_out));  // open: cin, cout
  Multiplier #(.width(4)) multiplier_11 (
    .a(bit_extender_11_out), .b(4'b1100), .out(multiplier_11_out));  // open: cin, cout
  Multiplier #(.width(4)) multiplier_12 (
    .a(bit_extender_12_out), .b(4'b1101), .out(multiplier_12_out));  // open: cin, cout
  Adder #(.width(4)) adder_1 (.a(bit_extender_13_out), .b(multiplier_1_out), .out(adder_1_out));  // open: cin, cout
  Adder #(.width(4)) adder_2 (.a(multiplier_2_out), .b(multiplier_3_out), .out(adder_2_out));  // open: cin, cout
  Adder #(.width(4)) adder_3 (.a(multiplier_4_out), .b(multiplier_5_out), .out(adder_3_out));  // open: cin, cout
  Adder #(.width(4)) adder_4 (.a(multiplier_6_out), .b(multiplier_7_out), .out(adder_4_out));  // open: cin, cout
  Adder #(.width(4)) adder_5 (.a(multiplier_8_out), .b(multiplier_9_out), .out(adder_5_out));  // open: cin, cout
  Adder #(.width(4)) adder_6 (.a(multiplier_10_out), .b(multiplier_11_out), .out(adder_6_out));  // open: cin, cout
  Adder #(.width(4)) adder_7 (.a(adder_1_out), .b(adder_2_out), .out(adder_7_out));  // open: cin, cout
  Adder #(.width(4)) adder_8 (.a(adder_3_out), .b(adder_4_out), .out(adder_8_out));  // open: cin, cout
  Adder #(.width(4)) adder_9 (.a(adder_5_out), .b(adder_6_out), .out(adder_9_out));  // open: cin, cout
  Adder #(.width(4)) adder_10 (.a(adder_7_out), .b(adder_8_out), .out(adder_10_out));  // open: cin, cout
  Adder #(.width(4)) adder_11 (.a(adder_9_out), .b(multiplier_12_out), .out(adder_11_out));  // open: cin, cout
  Adder #(.width(4)) adder_12 (.a(adder_10_out), .b(adder_11_out), .out(ALUSignals));  // open: cin, cout

  assign isImmediate = Instruction[26];

  // Notes on the sheet:
  //   Instruction: pull=down
  //   opcode
  //   (Circuit for signals created by multiple instructions)
  //   (Demultiplexer for Control Signals created by single instructions)
  //   Create ALUSignals
endmodule

module ALU (
  input  [31:0] A,
  input  [3:0] aluSignals,
  input  [31:0] B,
  input  clock,
  output [31:0] aluResult,
  output flags_GT,
  output flags_E
);

  wire [31:0] Add, addA, addB, And, andA, andB, Asr, asrA, asrB, cmpA, cmpB, Div, divA, divB, Lsl, lslA,
       lslB, Lsr, lsrA, lsrB, Mod, modA, modB, movB, Mul, mulA, mulB, Not, notB, Or, orA, orB, register_1_q,
       register_2_q, Sub, subA, subB;

  Demultiplexer #(.select(4), .width(32), .tristate("true"), .enable("false")) demultiplexer_1 (
    .out1(addA), .out2(subA), .out3(cmpA), .out4(mulA), .out5(divA), .out6(modA), .out7(lslA), .out8(lsrA),
    .out9(asrA), .out10(orA), .out12(andA), .in(A), .sel(aluSignals));  // open: out0, out11, out13, out14, out15
  Demultiplexer #(.select(4), .width(32), .tristate("true"), .disabled(0), .enable("false")) demultiplexer_2 (
    .out1(addB), .out2(subB), .out3(cmpB), .out4(mulB), .out5(divB), .out6(modB), .out7(lslB), .out8(lsrB),
    .out9(asrB), .out10(orB), .out11(notB), .out12(andB), .out13(movB), .in(B), .sel(aluSignals));  // open: out0, out14, out15
  Adder #(.width(32)) adder_1 (.a(addA), .b(addB), .out(Add));  // open: cin, cout
  Subtractor #(.width(32)) subtractor_1 (.a(subA), .b(subB), .out(Sub));  // open: bin, bout
  Shifter #(.width(32)) shifter_1 (.in(lslA), .\dist (lslB[4:0]), .out(Lsl));
  Shifter #(.width(32), .shift("lr")) shifter_2 (.in(lsrA), .\dist (lsrB[4:0]), .out(Lsr));
  Shifter #(.width(32), .shift("ar")) shifter_3 (.in(asrA), .\dist (asrB[4:0]), .out(Asr));
  Register #(.width(32)) register_1 (.D(cmpA), .Q(register_1_q), .clk(clock));  // open: en, clr
  Register #(.width(32)) register_2 (.D(cmpB), .Q(register_2_q), .clk(clock));  // open: en, clr
  Comparator #(.width(32)) comparator_1 (.a(register_1_q), .b(register_2_q), .gt(flags_GT), .eq(flags_E));  // open: lt
  Multiplier #(.width(32)) multiplier_1 (.a(mulA), .b(mulB), .out(Mul));  // open: cin, cout
  Divider #(.width(32)) divider_1 (.a(divA), .b(divB), .out(Div));  // open: upper, rem
  Divider #(.width(32)) divider_2 (.a(modA), .b(modB), .rem(Mod));  // open: out, upper
  Multiplexer #(.select(4), .width(32), .disabled(0)) multiplexer_1 (
    .in1(Add), .in2(Sub), .in4(Mul), .in5(Div), .in6(Mod), .in7(Lsl), .in8(Lsr), .in9(Asr), .in10(Or),
    .in11(Not), .in12(And), .in13(movB), .out(aluResult), .sel(aluSignals), .en(1'b1));  // open: in0, in3, in14, in15
  assign Or = orA | orB;  // OR_Gate or_1, 32 bits wide
  assign And = andA & andB;  // AND_Gate and_1, 32 bits wide
  assign Not = ~notB;  // NOT_Gate not_1, 32 bits wide

  // Notes on the sheet:
  //   flags_GT: pull=down
  //   B: pull=down
  //   aluResult: pull=down
  //   A: pull=down
  //   flags_E: pull=down
  //   Operand 1
  //   Operand 2
  //   Provide operands to their respective functions.
  //   Compare instruction needs registers as we need to keep the value of the flags stored.
endmodule

module EXU (
  input  isBeq,
  input  isUbranch,
  input  isBgt,
  input  isRet,
  input  [31:0] branchTargetIn,
  input  [31:0] A,
  input  [3:0] aluSignals,
  input  [31:0] B,
  input  Clock,
  output isBranchTaken,
  output [23:0] branchTargetOut,
  output [31:0] ALUResult
);

  wire and_1_out, and_2_out, flags_E, flags_GT;
  wire [31:24] multiplexer_1_out;

  and and_1 (and_1_out, isBeq, flags_E);
  and and_2 (and_2_out, isBgt, flags_GT);
  ALU alu_1 (
    .A(A), .aluSignals(aluSignals), .B(B), .clock(Clock), .aluResult(ALUResult), .flags_GT(flags_GT),
    .flags_E(flags_E));
  Multiplexer #(.width(32), .enable("false")) multiplexer_1 (
    .in0(branchTargetIn), .in1(A), .out({multiplexer_1_out, branchTargetOut}), .sel(isRet));
  or or_1 (isBranchTaken, and_1_out, isUbranch, and_2_out);

  // Notes on the sheet:
  //   isBranchTaken: pull=down
  //   aluSignals: pull=down
  //   isBeq: pull=down
  //   ALUResult: pull=down
  //   branchTargetOut: pull=down
  //   branchTargetIn: pull=down
  //   isUbranch: pull=down
  //   B: pull=down
  //   isBgt: pull=down
  //   A: pull=down
  //   (Operand 1)
  //   (Operand 2)
  //   EX Stage
  //   (To be sent to the IF Stage)
endmodule

module Forwarding_unit (
  input  [31:0] instr_A,
  input  [31:0] Insr_B,
  input  [31:0] RA,
  output isConflict,
  output FwdR2,
  output FwdR1
);

  wire comparator_1_eq, comparator_2_eq, comparator_3_eq, comparator_6_eq, comparator_7_eq, comparator_8_eq,
       comparator_9_eq, comparator_10_eq, comparator_11_eq, comparator_12_eq, comparator_13_eq,
       comparator_14_eq, comparator_15_eq, comparator_16_eq, comparator_17_eq, comparator_18_eq,
       comparator_19_eq, comparator_20_eq, isAbelongs, isBbelongs, noSrc1, noSrc2, not_1_out, not_3_out,
       not_4_out, or_2_out, or_5_out, SrcDestEq, SrcDestEq2;
  wire [3:0] multiplexer_3_out, rd_A, rd_B;
  wire [31:0] bit_extender_1_out, bit_extender_2_out, dest, ra_t, src1, src2;

  assign bit_extender_1_out = {{28{1'b0}}, instr_A[21:18]};  // Bit_Extender bit_extender_1
  Comparator #(.width(5)) comparator_1 (.a(instr_A[31:27]), .b(5'b10100), .eq(comparator_1_eq));  // open: gt, lt
  assign bit_extender_2_out = {{28{1'b0}}, rd_B};  // Bit_Extender bit_extender_2
  Comparator #(.width(5)) comparator_2 (.a(Insr_B[31:27]), .b(5'b10011), .eq(comparator_2_eq));  // open: gt, lt
  Comparator #(.width(5)) comparator_3 (.a(instr_A[31:27]), .b(5'b01111), .eq(comparator_3_eq));  // open: gt, lt
  Comparator #(.width(32)) comparator_4 (.a(src1), .b(dest), .eq(SrcDestEq));  // open: gt, lt
  Comparator #(.width(32)) comparator_5 (.a(src2), .b(dest), .eq(SrcDestEq2));  // open: gt, lt
  Multiplexer #(.width(32)) multiplexer_1 (
    .in0(bit_extender_1_out), .in1(ra_t), .out(src1), .sel(comparator_1_eq));  // open: en
  Multiplexer #(.width(32)) multiplexer_2 (
    .in0(bit_extender_2_out), .in1(ra_t), .out(dest), .sel(comparator_2_eq));  // open: en
  Multiplexer #(.width(4)) multiplexer_3 (
    .in0(instr_A[17:14]), .in1(rd_A), .out(multiplexer_3_out), .sel(comparator_3_eq));  // open: en
  assign src2 = {{28{1'b0}}, multiplexer_3_out};  // Bit_Extender bit_extender_3
  Comparator #(.width(5)) comparator_6 (.a(instr_A[31:27]), .b(5'b01101), .eq(comparator_6_eq));  // open: gt, lt
  Comparator #(.width(5)) comparator_7 (.a(instr_A[31:27]), .b(5'b10000), .eq(comparator_7_eq));  // open: gt, lt
  Comparator #(.width(5)) comparator_8 (.a(instr_A[31:27]), .b(5'b10001), .eq(comparator_8_eq));  // open: gt, lt
  Comparator #(.width(5)) comparator_9 (.a(instr_A[31:27]), .b(5'b10010), .eq(comparator_9_eq));  // open: gt, lt
  Comparator #(.width(5)) comparator_10 (.a(instr_A[31:27]), .b(5'b10011), .eq(comparator_10_eq));  // open: gt, lt
  Comparator #(.width(5)) comparator_11 (.a(Insr_B[31:27]), .b(5'b01101), .eq(comparator_11_eq));  // open: gt, lt
  Comparator #(.width(5)) comparator_12 (.a(Insr_B[31:27]), .b(5'b00101), .eq(comparator_12_eq));  // open: gt, lt
  Comparator #(.width(5)) comparator_13 (.a(Insr_B[31:27]), .b(5'b01111), .eq(comparator_13_eq));  // open: gt, lt
  Comparator #(.width(5)) comparator_14 (.a(Insr_B[31:27]), .b(5'b10000), .eq(comparator_14_eq));  // open: gt, lt
  Comparator #(.width(5)) comparator_15 (.a(Insr_B[31:27]), .b(5'b10001), .eq(comparator_15_eq));  // open: gt, lt
  Comparator #(.width(5)) comparator_16 (.a(Insr_B[31:27]), .b(5'b10010), .eq(comparator_16_eq));  // open: gt, lt
  Comparator #(.width(5)) comparator_17 (.a(Insr_B[31:27]), .b(5'b10100), .eq(comparator_17_eq));  // open: gt, lt
  Comparator #(.width(5)) comparator_18 (.a(instr_A[31:27]), .b(5'b01001), .eq(comparator_18_eq));  // open: gt, lt
  Comparator #(.width(5)) comparator_19 (.a(instr_A[31:27]), .b(5'b01000), .eq(comparator_19_eq));  // open: gt, lt
  Comparator #(.width(5)) comparator_20 (.a(instr_A[31:27]), .b(5'b01111), .eq(comparator_20_eq));  // open: gt, lt
  not not_1 (not_1_out, instr_A[26]);
  or or_1 (noSrc1, comparator_18_eq, comparator_19_eq);
  or or_2 (or_2_out, comparator_20_eq, not_1_out);
  not not_2 (noSrc2, or_2_out);
  or or_3 (isAbelongs, comparator_6_eq, comparator_7_eq, comparator_8_eq, comparator_9_eq, comparator_10_eq);
  or or_4 (isBbelongs, comparator_11_eq, comparator_12_eq, comparator_13_eq, comparator_14_eq, comparator_15_eq, comparator_16_eq, comparator_17_eq);
  not not_3 (not_3_out, noSrc2);
  not not_4 (not_4_out, noSrc1);
  or or_5 (or_5_out, isAbelongs, isBbelongs);
  not not_5 (isConflict, or_5_out);
  and and_1 (FwdR2, not_3_out, SrcDestEq2);
  and and_2 (FwdR1, SrcDestEq, not_4_out);

  // Other names for the same wires on the sheet: rs2_B[3:0] = Insr_B[17:14]; rs1_B[3:0] = Insr_B[21:18];
  //   rd_B_t[3:0] = Insr_B[25:22]; imm_B = Insr_B[26]; opc_B[4:0] = Insr_B[31:27]; rs2_A[3:0] = instr_A[17:14];
  //   rs1_A[3:0] = instr_A[21:18]; rd_A_t[3:0] = instr_A[25:22]; imm_A = instr_A[26]; opc_A[4:0] = instr_A[31:27]

  // Notes on the sheet:
  //   ret
  //   call
  //   st
  //   Nop
  //   beq
  //   bgt
  //   b
  //   call
  //   Nop
  //   cmp
  //   st
  //   beq
  //   bgt
  //   b
  //   ret
  //   mov
  //   not
  //   st
  //   if 1, ret false
  //   if 1, ret false
endmodule

module Data_lock_unit (
  input  [31:0] A_instruction,
  input  [31:0] B_instruction,
  input  clock,
  input  reset,
  output Is_conflict,
  output hasReached2,
  output hasReached1,
  output hasReached3
);

  wire A_I_1, A_I_t, A_opcode_call, A_opcode_end, A_opcode_mov, A_opcode_not, A_opcode_ret, A_opcode_st,
       and_1_out, and_2_out, and_3_out, and_4_out, B_opcode_call, B_opcode_end, comparator_2_eq,
       comparator_3_eq, comparator_4_eq, comparator_5_eq, comparator_9_eq, comparator_10_eq,
       comparator_11_eq, comparator_12_eq, comparator_13_eq, comparator_14_eq, comparator_15_eq,
       comparator_16_eq, comparator_17_eq, comparator_18_eq, comparator_19_eq, comparator_20_eq, hasSrc1,
       hasSrc2, not_1_out, not_2_out, not_3_out, not_4_out, or_1_out, or_2_out, or_3_out, read_and_write;
  wire [3:0] A_rd_t, A_rs1_t, A_rs2_t, B_rd_t, dest, dest_t, src1, src2;
  wire [4:0] st_t;
  wire [7:0] counter_1_q;

  Comparator #(.width(5)) comparator_1 (.a(A_instruction[31:27]), .b(5'b01000), .eq(A_opcode_not));  // open: gt, lt
  Multiplexer #(.width(4), .enable("false")) multiplexer_1 (.in0(A_rs2_t), .in1(A_rd_t), .out(src2), .sel(A_opcode_st));
  Multiplexer #(.width(4), .enable("false")) multiplexer_2 (
    .in0(A_rs1_t), .in1(4'b1111), .out(src1), .sel(A_opcode_ret));
  Multiplexer #(.width(4), .enable("false")) multiplexer_3 (
    .in0(B_rd_t), .in1(4'b1111), .out(dest_t), .sel(B_opcode_call));
  Comparator #(.width(1)) comparator_2 (.a(hasSrc1), .b(1'b1), .eq(comparator_2_eq));  // open: gt, lt
  Comparator #(.width(4)) comparator_3 (.a(src1), .b(dest), .eq(comparator_3_eq));  // open: gt, lt
  Comparator #(.width(1)) comparator_4 (.a(hasSrc2), .b(1'b1), .eq(comparator_4_eq));  // open: gt, lt
  Comparator #(.width(4)) comparator_5 (.a(src2), .b(dest_t), .eq(comparator_5_eq));  // open: gt, lt
  or or_1 (or_1_out, A_opcode_end, B_opcode_end);
  not not_1 (not_1_out, A_opcode_not);
  and and_1 (and_1_out, comparator_2_eq, comparator_3_eq);
  and and_2 (and_2_out, comparator_4_eq, comparator_5_eq);
  not not_2 (not_2_out, or_1_out);
  Counter counter_1 (.D({8{1'b0}}), .Q(counter_1_q), .clk(clock), .clr(reset));  // open: load, count, carry
  not not_3 (not_3_out, A_opcode_st);
  and and_3 (and_3_out, not_3_out, A_I_1);
  Multiplexer #(.enable("false")) multiplexer_4 (.in0(1'b1), .in1(1'b0), .out(hasSrc2), .sel(and_3_out));
  not not_4 (not_4_out, A_opcode_mov);
  and and_4 (and_4_out, not_1_out, not_4_out);
  or or_2 (or_2_out, and_1_out, and_2_out);
  Comparator comparator_6 (.a(counter_1_q), .b(8'h2), .gt(hasReached2));  // open: eq, lt
  Comparator comparator_7 (.a(counter_1_q), .b(8'h1), .gt(hasReached1));  // open: eq, lt
  Comparator comparator_8 (.a(counter_1_q), .b(8'h3), .gt(hasReached3));  // open: eq, lt
  Multiplexer #(.enable("false")) multiplexer_5 (.in0(1'b1), .in1(1'b0), .out(hasSrc1), .sel(and_4_out));
  and and_5 (Is_conflict, or_2_out, read_and_write, not_2_out, hasReached2);
  Comparator #(.width(5)) comparator_9 (.a(A_instruction[31:27]), .b(5'b01101), .eq(comparator_9_eq));  // open: gt, lt
  Comparator #(.width(5)) comparator_10 (
    .a(A_instruction[31:27]), .b(5'b10010), .eq(comparator_10_eq));  // open: gt, lt
  Comparator #(.width(5)) comparator_11 (
    .a(A_instruction[31:27]), .b(5'b10000), .eq(comparator_11_eq));  // open: gt, lt
  Comparator #(.width(5)) comparator_12 (
    .a(A_instruction[31:27]), .b(5'b01100), .eq(comparator_12_eq));  // open: gt, lt
  Comparator #(.width(5)) comparator_13 (
    .a(A_instruction[31:27]), .b(5'b10011), .eq(comparator_13_eq));  // open: gt, lt
  Comparator #(.width(5)) comparator_14 (
    .a(B_instruction[31:27]), .b(5'b01101), .eq(comparator_14_eq));  // open: gt, lt
  Comparator #(.width(5)) comparator_15 (
    .a(B_instruction[31:27]), .b(5'b00101), .eq(comparator_15_eq));  // open: gt, lt
  Comparator #(.width(5)) comparator_16 (
    .a(B_instruction[31:27]), .b(5'b01111), .eq(comparator_16_eq));  // open: gt, lt
  Comparator #(.width(5)) comparator_17 (
    .a(B_instruction[31:27]), .b(5'b10010), .eq(comparator_17_eq));  // open: gt, lt
  Comparator #(.width(5)) comparator_18 (
    .a(B_instruction[31:27]), .b(5'b10000), .eq(comparator_18_eq));  // open: gt, lt
  Comparator #(.width(5)) comparator_19 (
    .a(B_instruction[31:27]), .b(5'b01100), .eq(comparator_19_eq));  // open: gt, lt
  Comparator #(.width(5)) comparator_20 (
    .a(B_instruction[31:27]), .b(5'b10100), .eq(comparator_20_eq));  // open: gt, lt
  Comparator #(.width(5)) comparator_21 (.a(A_instruction[31:27]), .b(st_t), .eq(A_opcode_st));  // open: gt, lt
  Comparator #(.width(5)) comparator_22 (.a(A_instruction[31:27]), .b(5'b10100), .eq(A_opcode_ret));  // open: gt, lt
  Comparator #(.width(5)) comparator_23 (.a(B_instruction[31:27]), .b(5'b10011), .eq(B_opcode_call));  // open: gt, lt
  Comparator #(.width(1)) comparator_24 (.a(A_I_t), .b(1'b1), .eq(A_I_1));  // open: gt, lt
  Comparator #(.width(5)) comparator_25 (.a(A_instruction[31:27]), .b(5'b01001), .eq(A_opcode_mov));  // open: gt, lt
  Comparator #(.width(5)) comparator_26 (.a(B_instruction[31:27]), .b(5'b01000), .eq(A_opcode_call));  // open: gt, lt
  or or_3 (or_3_out, comparator_9_eq, comparator_10_eq, comparator_11_eq, comparator_12_eq, comparator_13_eq, comparator_14_eq, comparator_15_eq, comparator_16_eq, comparator_17_eq, comparator_18_eq, comparator_19_eq, comparator_20_eq);
  not not_5 (read_and_write, or_3_out);
  Comparator #(.width(5)) comparator_27 (.a(A_instruction[31:27]), .b(5'b00111), .eq(A_opcode_end));  // open: gt, lt
  Comparator #(.width(5)) comparator_28 (.a(B_instruction[31:27]), .b(5'b00111), .eq(B_opcode_end));  // open: gt, lt

  // Other names for the same wires on the sheet: A_rs2[3:0] = A_instruction[17:14]; A_rs1[3:0] = A_instruction[21:18];
  //   A_rd[3:0] = A_instruction[25:22]; A_I = A_instruction[26]; A_opcode[4:0] = A_instruction[31:27];
  //   B_rs2[3:0] = B_instruction[17:14]; B_rs1[3:0] = B_instruction[21:18]; B_rd[3:0] = B_instruction[25:22];
  //   B_I = B_instruction[26]; B_opcode[4:0] = B_instruction[31:27]

  // Notes on the sheet:
  //   Set Sources
  //   Set destination
  //   Set destination
  //   Check Second if Register
  //   Check Second if Register
endmodule
